// Logisim project au.circ as structural Verilog: 1 circuit, main circuit ALU
module ALU (
  input  [31:0] reg1,
  input  [31:0] reg2,
  input  [4:0] shiftAmount,
  input  [3:0] operation,
  input  isShiftAmount,
  input  [2:0] branchType,
  output [31:0] result,
  output zero
);

  wire comparator_1_eq, comparator_1_gt, comparator_1_lt, comparator_2_eq, not_1_out, or_1_out, or_2_out;
  wire [0:0] comparator_2_lt;
  wire [4:0] multiplexer_1_out, multiplexer_2_out;
  wire [31:0] adder_1_out, and_1_out, divider_1_out, multiplier_1_out, nor_1_out, or_3_out, shifter_1_out,
       shifter_2_out, shifter_3_out, shifter_4_out, subtractor_1_out, undriven, undriven_2, xor_1_out;

  Comparator #(.width(32)) comparator_1 (
    .a(reg1), .b({32{1'b0}}), .gt(comparator_1_gt), .eq(comparator_1_eq), .lt(comparator_1_lt));
  Multiplexer #(.width(5)) multiplexer_1 (
    .in0(reg1[4:0]), .in1(shiftAmount), .out(multiplexer_1_out), .sel(isShiftAmount));
  Multiplexer #(.width(5)) multiplexer_2 (
    .in0(reg1[4:0]), .in1(shiftAmount), .out(multiplexer_2_out), .sel(isShiftAmount));
  or or_1 (or_1_out, comparator_1_eq, comparator_1_lt);
  or or_2 (or_2_out, comparator_1_eq, comparator_1_gt);
  Adder #(.width(32)) adder_1 (.a(reg1), .b(reg2), .out(adder_1_out));  // open: cin, cout
  Subtractor #(.width(32)) subtractor_1 (.a(reg1), .b(reg2), .out(subtractor_1_out));  // open: bin, bout
  assign xor_1_out = reg1 ^ reg2;  // XOR_Gate xor_1, 32 bits wide
  assign and_1_out = reg1 & reg2;  // AND_Gate and_1, 32 bits wide
  assign or_3_out = reg1 | reg2;  // OR_Gate or_3, 32 bits wide
  assign nor_1_out = ~(reg1 | reg2);  // NOR_Gate nor_1, 32 bits wide
  Multiplier #(.width(32)) multiplier_1 (.a(reg1), .b(reg2), .out(multiplier_1_out));  // open: cin, cout
  Divider #(.width(32)) divider_1 (.a(reg1), .b(reg2), .out(divider_1_out));  // open: upper, rem
  Shifter #(.width(32)) shifter_1 (.in(reg2), .\dist (multiplexer_1_out), .out(shifter_1_out));
  Shifter #(.shift("lr"), .width(32)) shifter_2 (.in(reg2), .\dist (multiplexer_2_out), .out(shifter_2_out));
  Shifter #(.shift("ar"), .width(32)) shifter_3 (.in(reg2), .\dist (shiftAmount), .out(shifter_3_out));
  Comparator #(.width(32)) comparator_2 (
    .a(reg1), .b(reg2), .eq(comparator_2_eq), .lt(comparator_2_lt[0]));  // open: gt
  Shifter #(.width(32)) shifter_4 (.in(reg2), .\dist (5'b10000), .out(shifter_4_out));
  not not_1 (not_1_out, comparator_2_eq);
  Multiplexer #(.select(3)) multiplexer_3 (
    .in1(or_2_out), .in4(comparator_2_eq), .in5(not_1_out), .in6(or_1_out), .in7(comparator_1_gt),
    .out(zero), .sel(branchType));  // open: in0, in2, in3
  Multiplexer #(.select(4), .width(32)) multiplexer_4 (
    .in0(adder_1_out), .in1(undriven), .in2(subtractor_1_out), .in3(undriven_2), .in4(xor_1_out),
    .in5(and_1_out), .in6(or_3_out), .in7(nor_1_out), .in8(multiplier_1_out), .in9(divider_1_out),
    .in10(shifter_1_out), .in11(shifter_2_out), .in12(shifter_3_out),
    .in13({{31{1'b0}}, comparator_2_lt[0]}), .in14(reg1), .in15(shifter_4_out), .out(result), .sel(operation));

  // Notes on the sheet:
  //   inputs
  //   Adder
  //   Unsigned Adder
  //   Subtractor
  //   Unsigned Subtractor
  //   XOR
  //   AND
  //   OR
  //   NOR
  //   Multiplier
  //   Divider
  //   Logical Left
  //   Logical Right
  //   Arithmatic Right
  //   Comprator
  //   000100
  //   000101
  //   000110
  //   000111
  //   000001
  //   001000
  //   001111
  //   000000 for shiftAmount
  //   000100 for variable
  //   100000
  //   100001
  //   100010
  //   100011
  //   100110
  //   100100
  //   100101
  //   100111
  //   011000
  //   011010
  //   000010 for shiftAmount unsigned
  //   000110 for variable
  //   000011
  //   001000
  //   001001
  //   001110
  //   001100
  //   001101
  //   101010
  //   100011
  //   101011
  //   100000
  //   101000
  //   001010
  //   from control
endmodule
